# Fritzing sketch circuit (saved by Fritzing 0.9.3b)
breadboards: 1

parts:
  Part1 = Arduino Mega 2560 (Rev3)
  U2 = Battery Holders [package=battery-aa-kit]
  U3 = Battery Holders [package=battery-aa-kit]
  U6 = Battery Holders [package=battery-aa-kit]
  DS1 = DS18B20 1-Wire Temperature Sensor [part_number=DS18B20]
  R1 = Resistor [tolerance=±5% resistance=4.7k package="0603 [SMD]"]
  R2 = Resistor [tolerance=±5% resistance=100k package="0603 [SMD]"]
  R3 = Resistor [tolerance=±5% resistance=1k package="0603 [SMD]"]

nets:
  5V: Part1.5V, DS1.VDD, R1.Pin_0
  GND: Part1.GND, U3.-, DS1.GND, R3.Pin_0
  N1: Part1.D49, R2.Pin_0, R3.Pin_1
  N2: Part1.D53, DS1.DQ, R1.Pin_1
  N3: U2.+, U6.-
  N4: U2.-, U3.+
  N5: U6.+, R2.Pin_1
